// Logisim project CPS213 Lab 3 Problem 1 NOR.circ as structural Verilog: 1 circuit, main circuit main
module main (
  input  w,
  input  x,
  input  y,
  input  z,
  output F
);

  wire not_1_out, not_2_out, not_3_out, not_4_out, not_5_out, or_1_out, or_2_out, or_3_out;

  not not_1 (not_1_out, y);
  or or_1 (or_1_out, not_1_out, not_2_out);
  not not_2 (not_2_out, z);
  not not_3 (not_3_out, x);
  or or_2 (or_2_out, not_3_out, z);
  not not_4 (not_4_out, w);
  or or_3 (or_3_out, not_4_out, x, not_5_out);
  not not_5 (not_5_out, z);
  and and_1 (F, or_1_out, or_2_out, or_3_out);
endmodule
