// Logisim project CPS213 Lab 3 Problem 2 Minterm.circ as structural Verilog: 1 circuit, main circuit main
module main (
  input  w,
  input  x,
  input  y,
  input  z,
  output F
);

  wire and_1_out, and_2_out, and_3_out, not_1_out, not_2_out, not_3_out, not_4_out, not_5_out, not_6_out;

  not not_1 (not_1_out, w);
  and and_1 (and_1_out, not_1_out, not_2_out, not_3_out);
  not not_2 (not_2_out, x);
  not not_3 (not_3_out, y);
  not not_4 (not_4_out, x);
  and and_2 (and_2_out, not_4_out, not_5_out);
  not not_5 (not_5_out, z);
  not not_6 (not_6_out, y);
  and and_3 (and_3_out, x, not_6_out, z);
  or or_1 (F, and_1_out, and_2_out, and_3_out);
endmodule
