// Logisim project Lab 5 CPS213.circ as structural Verilog: 12 circuits, main circuit ALU
module ALU (
  input  Cin,
  input  Enable,
  input  [3:0] in_3,
  input  [3:0] A,
  input  [3:0] B,
  input  M,
  input  [1:0] S0,
  output C0,
  output C1,
  output [3:0] out_10,
  output A___B,
  output A___B_2,
  output B___A
);

  wire Binary_to_Hexadecimal_LED_a, Binary_to_Hexadecimal_LED_b, Binary_to_Hexadecimal_LED_c,
       Binary_to_Hexadecimal_LED_d, Binary_to_Hexadecimal_LED_e, Binary_to_Hexadecimal_LED_f,
       Binary_to_Hexadecimal_LED_g, not_1_out;
  wire [3:0] Arithmetic_Unit_p8, Logic_f;

  // Arithmetic_Unit Arithmetic_Unit: pin names not known; wires that end beside it: Cin, A, S0, B, in_3, C0, C1, Arithmetic_Unit_p8
  Comparator_Unit Comparator (.A(A), .B(B), .A___B(A___B), .A___B_2(A___B_2), .A___B_3(B___A));
  not not_1 (not_1_out, Enable);
  Logic_Unit Logic (.A(A), .F(Logic_f), .B(B), .S0S1(S0), .Enable(not_1_out));
  Multiplexer #(.width(4), .enable("false")) multiplexer_1 (
    .in0(Arithmetic_Unit_p8), .in1(Logic_f), .out(out_10), .sel(M));
  LED Binary_to_Hexadecimal_LED (
    .w(out_10[3]), .x(out_10[2]), .y(out_10[1]), .z(out_10[0]), .a(Binary_to_Hexadecimal_LED_a),
    .b(Binary_to_Hexadecimal_LED_b), .c(Binary_to_Hexadecimal_LED_c), .d(Binary_to_Hexadecimal_LED_d),
    .e(Binary_to_Hexadecimal_LED_e), .f(Binary_to_Hexadecimal_LED_f), .g(Binary_to_Hexadecimal_LED_g));
  _7_Segment_Display u_7_segment_display_1 (
    .g(Binary_to_Hexadecimal_LED_g), .f(Binary_to_Hexadecimal_LED_f), .a(Binary_to_Hexadecimal_LED_a),
    .b(Binary_to_Hexadecimal_LED_b), .e(Binary_to_Hexadecimal_LED_e), .d(Binary_to_Hexadecimal_LED_d),
    .c(Binary_to_Hexadecimal_LED_c));  // open: dp
endmodule

module Logic_Unit (
  input  [3:0] A,
  input  [3:0] B,
  input  [1:0] S0S1,
  input  Enable,
  output [3:0] F
);

  wire [3:0] and_circuit_1_out_9, n1_s_comp_1_out_5, or_1_out_9, xor_1_out_9;

  _1_s_COMP u_1_s_comp_1 (
    .A0(A[0]), .A1(A[1]), .A2(A[2]), .A3(A[3]), .out_5(n1_s_comp_1_out_5[0]), .out_6(n1_s_comp_1_out_5[1]),
    .out_7(n1_s_comp_1_out_5[2]), .out_8(n1_s_comp_1_out_5[3]));
  AND_circuit and_circuit_1 (
    .A0(A[0]), .B0(B[0]), .A1(A[1]), .B1(B[1]), .A2(A[2]), .B2(B[2]), .A3(A[3]), .B3(B[3]),
    .out_9(and_circuit_1_out_9[0]), .out_10(and_circuit_1_out_9[1]), .out_11(and_circuit_1_out_9[2]),
    .out_12(and_circuit_1_out_9[3]));
  OR or_1 (
    .A0(A[0]), .B0(B[0]), .A1(A[1]), .B1(B[1]), .A2(A[2]), .B2(B[2]), .A3(A[3]), .B3(B[3]),
    .out_9(or_1_out_9[0]), .out_10(or_1_out_9[1]), .out_11(or_1_out_9[2]), .out_12(or_1_out_9[3]));
  XOR xor_1 (
    .A0(A[0]), .B0(B[0]), .A1(A[1]), .B1(B[1]), .A2(A[2]), .B2(B[2]), .A3(A[3]), .B3(B[3]),
    .out_9(xor_1_out_9[0]), .out_10(xor_1_out_9[1]), .out_11(xor_1_out_9[2]), .out_12(xor_1_out_9[3]));
  Multiplexer #(.select(2), .width(4)) multiplexer_1 (
    .in0(and_circuit_1_out_9), .in1(or_1_out_9), .in2(xor_1_out_9), .in3(n1_s_comp_1_out_5), .out(F),
    .sel(S0S1), .en(Enable));
endmodule

// AND
module AND_circuit (
  input  A0,
  input  B0,
  input  A1,
  input  B1,
  input  A2,
  input  B2,
  input  A3,
  input  B3,
  output out_9,
  output out_10,
  output out_11,
  output out_12
);

  and and_1 (out_9, A0, B0);
  and and_2 (out_10, A1, B1);
  and and_3 (out_11, A2, B2);
  and and_4 (out_12, A3, B3);
endmodule

module OR (
  input  A0,
  input  B0,
  input  A1,
  input  B1,
  input  A2,
  input  B2,
  input  A3,
  input  B3,
  output out_9,
  output out_10,
  output out_11,
  output out_12
);

  or or_1 (out_9, A0, B0);
  or or_2 (out_10, A1, B1);
  or or_3 (out_11, A2, B2);
  or or_4 (out_12, A3, B3);
endmodule

module XOR (
  input  A0,
  input  B0,
  input  A1,
  input  B1,
  input  A2,
  input  B2,
  input  A3,
  input  B3,
  output out_9,
  output out_10,
  output out_11,
  output out_12
);

  xor xor_1 (out_9, A0, B0);
  xor xor_2 (out_10, A1, B1);
  xor xor_3 (out_11, A2, B2);
  xor xor_4 (out_12, A3, B3);
endmodule

module _1_s_COMP (
  input  A0,
  input  A1,
  input  A2,
  input  A3,
  output out_5,
  output out_6,
  output out_7,
  output out_8
);

  not not_1 (out_5, A0);
  not not_2 (out_6, A1);
  not not_3 (out_7, A2);
  not not_4 (out_8, A3);
endmodule

module Arithmetic_Unit (
  input  Carry_in,
  input  [3:0] A,
  input  [3:0] B,
  input  [1:0] s0s1,
  input  Enable,
  input  [3:0] A1,
  input  Carry_in_2,
  input  [3:0] Increment,
  output C0,
  output [3:0] F,
  output C1,
  output C2,
  output C3
);

  wire not_1_out;
  wire [3:0] _2_s_Complement_f, _4_bit_Full_Adder_2_f, _4_bit_Full_Adder_f, _4_bit_Subtractor_f;

  not not_1 (not_1_out, Carry_in);
  _4_bit_full_adder _4_bit_Full_Adder (.Cin(Carry_in), .F(_4_bit_Full_Adder_f), .A(A), .B(B), .Carry_out_c0(C0));
  _4_bit_Subtractor _4_bit_Subtractor (.F(_4_bit_Subtractor_f), .A(A), .B(B), .Cin(not_1_out), .Cout(C1));
  _4_bit_Subtractor _2_s_Complement (.F(_2_s_Complement_f), .A(A1), .B(B), .Cin(not_1_out), .Cout(C2));
  _4_bit_full_adder _4_bit_Full_Adder_2 (
    .Cin(Carry_in_2), .F(_4_bit_Full_Adder_2_f), .A(A), .B(Increment), .Carry_out_c0(C3));
  Multiplexer #(.select(2), .width(4)) multiplexer_1 (
    .in0(_4_bit_Full_Adder_f), .in1(_4_bit_Subtractor_f), .in2(_2_s_Complement_f),
    .in3(_4_bit_Full_Adder_2_f), .out(F), .sel(s0s1), .en(Enable));
endmodule

module _1_bit_full_adder (
  input  A,
  input  B,
  input  Carry_In,
  output Sum,
  output Carry_out_c0
);

  wire Addition_out, Carry_2_out, Carry_out;

  xor Addition (Addition_out, A, B);
  and Carry (Carry_out, A, B);
  xor xor_1 (Sum, Addition_out, Carry_In);
  and Carry_2 (Carry_2_out, Addition_out, Carry_In);
  or or_1 (Carry_out_c0, Carry_2_out, Carry_out);
endmodule

module _4_bit_full_adder (
  input  Cin,
  input  [3:0] A,
  input  [3:0] B,
  output [3:0] F,
  output Carry_out_c0
);

  wire n1_bit_full_adder_1_carry_out_c0, n1_bit_full_adder_2_carry_out_c0, n1_bit_full_adder_3_carry_out_c0;

  _1_bit_full_adder u_1_bit_full_adder_1 (
    .A(A[0]), .B(B[0]), .Carry_In(Cin), .Sum(F[0]), .Carry_out_c0(n1_bit_full_adder_1_carry_out_c0));
  _1_bit_full_adder u_1_bit_full_adder_2 (
    .A(A[1]), .B(B[1]), .Carry_In(n1_bit_full_adder_1_carry_out_c0), .Sum(F[1]),
    .Carry_out_c0(n1_bit_full_adder_2_carry_out_c0));
  _1_bit_full_adder u_1_bit_full_adder_3 (
    .A(A[2]), .B(B[2]), .Carry_In(n1_bit_full_adder_2_carry_out_c0), .Sum(F[2]),
    .Carry_out_c0(n1_bit_full_adder_3_carry_out_c0));
  _1_bit_full_adder u_1_bit_full_adder_4 (
    .A(A[3]), .B(B[3]), .Carry_In(n1_bit_full_adder_3_carry_out_c0), .Sum(F[3]), .Carry_out_c0(Carry_out_c0));
endmodule

module _4_bit_Subtractor (
  input  Cin,
  input  [3:0] A,
  input  [3:0] B,
  output [3:0] F,
  output Cout
);

  wire _1_bit_full_adder_carry_out_c0, n1_bit_full_adder_1_carry_out_c0, n1_bit_full_adder_2_carry_out_c0,
       not_1_out, not_2_out, not_3_out, not_4_out;

  not not_1 (not_1_out, B[0]);
  not not_2 (not_2_out, B[3]);
  not not_3 (not_3_out, B[1]);
  not not_4 (not_4_out, B[2]);
  _1_bit_full_adder _1_bit_full_adder (
    .A(A[0]), .B(not_1_out), .Carry_In(Cin), .Sum(F[0]), .Carry_out_c0(_1_bit_full_adder_carry_out_c0));
  _1_bit_full_adder u_1_bit_full_adder_1 (
    .A(A[1]), .B(not_3_out), .Carry_In(_1_bit_full_adder_carry_out_c0), .Sum(F[1]),
    .Carry_out_c0(n1_bit_full_adder_1_carry_out_c0));
  _1_bit_full_adder u_1_bit_full_adder_2 (
    .A(A[2]), .B(not_4_out), .Carry_In(n1_bit_full_adder_1_carry_out_c0), .Sum(F[2]),
    .Carry_out_c0(n1_bit_full_adder_2_carry_out_c0));
  _1_bit_full_adder u_1_bit_full_adder_3 (
    .A(A[3]), .B(not_2_out), .Carry_In(n1_bit_full_adder_2_carry_out_c0), .Sum(F[3]), .Carry_out_c0(Cout));
endmodule

module Comparator_Unit (
  input  [3:0] A,
  input  [3:0] B,
  output A___B,
  output A___B_2,
  output A___B_3
);

  wire and_1_out, and_2_out, and_3_out, and_4_out, and_5_out, and_6_out, and_7_out, and_8_out, and_10_out,
       and_11_out, and_12_out, and_13_out, and_14_out, and_15_out, nor_1_out, nor_2_out, nor_3_out,
       nor_4_out, not_1_out, not_2_out, not_3_out, not_4_out, not_5_out, not_6_out, not_7_out, not_8_out;

  not not_1 (not_1_out, A[0]);
  not not_2 (not_2_out, B[0]);
  not not_3 (not_3_out, A[1]);
  not not_4 (not_4_out, B[1]);
  not not_5 (not_5_out, A[2]);
  not not_6 (not_6_out, B[2]);
  not not_7 (not_7_out, A[3]);
  not not_8 (not_8_out, B[3]);
  and and_1 (and_1_out, B[0], not_1_out);
  and and_2 (and_2_out, not_2_out, A[0]);
  and and_3 (and_3_out, B[1], not_3_out);
  and and_4 (and_4_out, not_4_out, A[1]);
  and and_5 (and_5_out, B[2], not_5_out);
  and and_6 (and_6_out, not_6_out, A[2]);
  and and_7 (and_7_out, B[3], not_7_out);
  and and_8 (and_8_out, not_8_out, A[3]);
  nor nor_1 (nor_1_out, and_1_out, and_2_out);
  nor nor_2 (nor_2_out, and_3_out, and_4_out);
  nor nor_3 (nor_3_out, and_5_out, and_6_out);
  nor nor_4 (nor_4_out, and_7_out, and_8_out);
  and and_9 (A___B, nor_1_out, nor_2_out, nor_3_out, nor_4_out);
  and and_10 (and_10_out, and_2_out, nor_2_out, nor_3_out, nor_4_out);
  and and_11 (and_11_out, and_1_out, nor_2_out, nor_3_out, nor_4_out);
  and and_12 (and_12_out, and_4_out, nor_3_out, nor_4_out);
  and and_13 (and_13_out, nor_4_out, nor_3_out, and_3_out);
  and and_14 (and_14_out, and_6_out, nor_4_out);
  and and_15 (and_15_out, and_5_out, nor_4_out);
  or or_1 (A___B_2, and_8_out, and_14_out, and_12_out, and_10_out);
  or or_2 (A___B_3, and_7_out, and_15_out, and_13_out, and_11_out);
endmodule

module LED (
  input  w,
  input  x,
  input  y,
  input  z,
  output a,
  output b,
  output c,
  output d,
  output e,
  output f,
  output g
);

  wire and_1_out, and_2_out, and_3_out, and_4_out, and_5_out, and_6_out, and_7_out, and_8_out, and_9_out,
       and_10_out, and_11_out, and_12_out, and_13_out, and_14_out, and_15_out, and_16_out, and_17_out,
       and_18_out, and_19_out, and_20_out, and_21_out, and_22_out, and_23_out, and_24_out, and_25_out,
       and_26_out, and_27_out, and_28_out, and_29_out, and_30_out, and_31_out, and_32_out, and_33_out,
       and_34_out, and_35_out, not_1_out, not_2_out, not_3_out, not_4_out, not_5_out, not_6_out, not_7_out,
       not_8_out, not_9_out, not_10_out, not_11_out, not_12_out, not_13_out, not_14_out, not_15_out,
       not_16_out, not_17_out, not_18_out, not_19_out, not_20_out, not_21_out, not_22_out, not_23_out,
       not_24_out, not_25_out, not_26_out, not_27_out, not_28_out, not_29_out, not_30_out, not_31_out,
       not_32_out, not_33_out, not_34_out, not_35_out, not_36_out, not_37_out, not_38_out, not_39_out,
       not_40_out, not_41_out, not_42_out, not_43_out;

  not not_1 (not_1_out, x);
  and and_1 (and_1_out, not_1_out, not_2_out);
  not not_2 (not_2_out, z);
  not not_3 (not_3_out, w);
  and and_2 (and_2_out, not_3_out, y);
  not not_4 (not_4_out, w);
  and and_3 (and_3_out, not_4_out, x, z);
  and and_4 (and_4_out, x, y);
  and and_5 (and_5_out, w, not_5_out, not_6_out);
  not not_5 (not_5_out, x);
  not not_6 (not_6_out, y);
  and and_6 (and_6_out, w, not_7_out);
  not not_7 (not_7_out, z);
  not not_8 (not_8_out, w);
  and and_7 (and_7_out, not_8_out, not_9_out);
  not not_9 (not_9_out, x);
  not not_10 (not_10_out, w);
  not not_11 (not_11_out, y);
  and and_8 (and_8_out, not_10_out, not_11_out, not_12_out);
  not not_12 (not_12_out, z);
  not not_13 (not_13_out, x);
  and and_9 (and_9_out, not_13_out, not_14_out);
  not not_14 (not_14_out, z);
  not not_15 (not_15_out, w);
  and and_10 (and_10_out, not_15_out, y, z);
  and and_11 (and_11_out, w, not_16_out, z);
  not not_16 (not_16_out, y);
  not not_17 (not_17_out, w);
  and and_12 (and_12_out, not_17_out, not_18_out);
  not not_18 (not_18_out, y);
  not not_19 (not_19_out, w);
  and and_13 (and_13_out, not_19_out, z);
  not not_20 (not_20_out, y);
  and and_14 (and_14_out, not_20_out, z);
  not not_21 (not_21_out, w);
  and and_15 (and_15_out, not_21_out, x);
  and and_16 (and_16_out, w, not_22_out);
  not not_22 (not_22_out, x);
  not not_23 (not_23_out, w);
  and and_17 (and_17_out, not_23_out, not_24_out, not_25_out);
  not not_24 (not_24_out, x);
  not not_25 (not_25_out, z);
  not not_26 (not_26_out, x);
  and and_18 (and_18_out, not_26_out, y, z);
  not not_27 (not_27_out, y);
  and and_19 (and_19_out, x, not_27_out, z);
  and and_20 (and_20_out, x, y, not_28_out);
  not not_28 (not_28_out, z);
  and and_21 (and_21_out, w, not_29_out);
  not not_29 (not_29_out, y);
  not not_30 (not_30_out, x);
  and and_22 (and_22_out, not_30_out, not_31_out);
  not not_31 (not_31_out, z);
  and and_23 (and_23_out, y, not_32_out);
  not not_32 (not_32_out, z);
  and and_24 (and_24_out, w, y);
  and and_25 (and_25_out, w, x);
  not not_33 (not_33_out, y);
  and and_26 (and_26_out, not_33_out, not_34_out);
  not not_34 (not_34_out, z);
  not not_35 (not_35_out, w);
  and and_27 (and_27_out, not_35_out, x, not_36_out);
  not not_36 (not_36_out, y);
  and and_28 (and_28_out, x, not_37_out);
  not not_37 (not_37_out, z);
  and and_29 (and_29_out, w, not_38_out);
  not not_38 (not_38_out, x);
  and and_30 (and_30_out, w, y);
  not not_39 (not_39_out, x);
  and and_31 (and_31_out, not_39_out, y);
  and and_32 (and_32_out, y, not_40_out);
  not not_40 (not_40_out, z);
  not not_41 (not_41_out, w);
  and and_33 (and_33_out, not_41_out, x, not_42_out);
  not not_42 (not_42_out, y);
  and and_34 (and_34_out, w, not_43_out);
  not not_43 (not_43_out, x);
  and and_35 (and_35_out, w, z);
  or or_1 (b, and_7_out, and_8_out, and_9_out, and_10_out, and_11_out);
  or or_2 (c, and_12_out, and_13_out, and_14_out, and_15_out, and_16_out);
  or or_3 (d, and_17_out, and_18_out, and_19_out, and_20_out, and_21_out);
  or or_4 (e, and_22_out, and_23_out, and_24_out, and_25_out);
  or or_5 (f, and_26_out, and_27_out, and_28_out, and_29_out, and_30_out);
  or or_6 (g, and_31_out, and_32_out, and_33_out, and_34_out, and_35_out);
  or or_7 (a, and_1_out, and_2_out, and_3_out, and_4_out, and_5_out, and_6_out);
  _7_Segment_Display u_7_segment_display_1 (.g(g), .f(f), .a(a), .b(b), .e(e), .d(d), .c(c));  // open: dp
endmodule
